# Fritzing sketch C3daughter_board (saved by Fritzing 0.8.3b)
breadboards: 1

parts:
  Propeller1 = Parallax Propeller D40 [package="DIP [THT]"]
  VCC1 = Battery
  VCC2 = Battery
  J1 = Screw terminal - 2 pins [package=THT]
  J3 = female pin header, 4 pins [form="♀ (female)"]
  S1 = Toggle Switch [package=THT]
  LED1 = LED - 5mm [color="Red (633nm)" package="5 mm [THT]"]
  R4 = Resistor [tolerance=±5% resistance=470 package=THT]
  J4 = Screw terminal - 2 pins [package=THT]
  J2 = shrouded pin header, 10 pins [form="♂ (shrouded male)"]
  R5 = Resistor [tolerance=±5% resistance=4.7k package=THT]

nets:
  N1: Propeller1.P0, R5.Pin_0
  N2: Propeller1.P1, R4.Pin_1
  N3: Propeller1.P4, J2.pin2, J2.pin9
  N4: Propeller1.P5, J2.pin3, J2.pin8
  N5: Propeller1.P6, J2.pin7
  N6: Propeller1.P7, J2.pin4
  N7: Propeller1.P28, J3.pin3
  N8: Propeller1.P29, J3.pin4
  N9: VCC1.-, VCC2.-, J3.pin1, S1.COM, J2.pin5, J2.pin6
  N10: VCC1.+, J1.pin2, J2.pin1
  N11: VCC2.+, J3.pin2
  N12: J1.pin1, R5.Pin_1
  N13: S1.L2, LED1.cathode
  N14: LED1.anode, R4.Pin_0
  N15: J4.pin1, J2.pin10

notes:
  5V
  ChronoDot I2C DS3231
  DIOB Serial Interface
