# Fritzing sketch ups_board (saved by Fritzing 0.8.3b)
breadboards: 1

parts:
  VCC1 = Battery
  D1 = Rectifier Diode [part_number=1N4007 package="300 mil [THT]"]
  D2 = Rectifier Diode [part_number=1N4007 package="300 mil [THT]"]
  D3 = Rectifier Diode [part_number=1N4007 package="300 mil [THT]"]
  D4 = Rectifier Diode [part_number=1N4007 package="300 mil [THT]"]
  R1 = Resistor [tolerance=±5% resistance=2.2k power=2W package=THT]
  D5 = Rectifier Diode [part_number=1N4001 package="300 mil [THT]"]
  D6 = Rectifier Diode [part_number=1N4001 package="300 mil [THT]"]
  U1 = Voltage Regulator - 5V [part_number=MC78T12 package="TO220 [THT]"]
  Q1 = PNP-Transistor [package="TO92 [THT]"]
  R2 = Resistor [tolerance=±5% resistance=220 package=THT]
  12V_Li-Ion_Battery = Screw terminal - 2 pins [package=THT]
  R3 = Resistor [tolerance=±5% resistance=220 package=THT]
  J2_-_12V_DC_out = Screw terminal - 2 pins [package=THT]
  LED2 = LED - 5mm [color="Green (565nm)" package="5 mm [THT]"]
  R4 = Resistor [tolerance=±5% resistance=220 package=THT]
  LED3 = LED - 5mm [color="Red (633nm)" package="5 mm [THT]"]
  IC1 = IC, DIP package, 8 pins [chip_label=IC741]
  Q2 = NPN-Transistor [package="TO92 [THT]"]

nets:
  N1: VCC1.-, D4.cathode, R2.Pin_1, R3.Pin_1, J2_-_12V_DC_out.pin2, LED2.anode, IC1.pin4
  N2: VCC1.+, U1.input_voltage
  N3: D1.cathode, D4.anode
  N4: D1.anode, D3.cathode
  N5: D2.cathode, D3.anode
  N6: D2.anode, R1.Pin_0, U1.GND
  N7: R1.Pin_1, D6.anode, U1.output_voltage, Q1.E
  N8: D5.cathode, J2_-_12V_DC_out.pin1
  N9: D5.anode, D6.cathode
  N10: Q1.B, LED3.cathode
  N11: Q1.C, 12V_Li-Ion_Battery.pin1
  N12: R3.Pin_0, LED2.cathode
  N13: R4.Pin_0, LED3.anode
  N14: R4.Pin_1, IC1.pin6
  N15: IC1.pin2, Q2.E
