# Fritzing sketch ups (saved by Fritzing 0.8.7b)
breadboards: 1

parts:
  19V_DC = Screw terminal - 2 pins [package=THT]
  C1 = Ceramic Capacitor [capacitance=100nF package="100 mil [THT, multilayer]"]
  U1 = Voltage Regulator - Variable [package="TO220 [THT]"]
  R1 = Resistor [tolerance=±5% resistance=120 package=THT]
  R2 = Trimmer Potentiometer [maximum_resistance=100kΩ package=THT]

nets:
  N1: 19V_DC.pin1, C1.1, U1.IN
  GND: 19V_DC.pin2, C1.0, R2.wiper, R2.leg2
  N2: U1.ADJ, R1.Pin_0, R2.leg1
  N3: U1.OUT, R1.Pin_1
